// Logisim project 10b.circ as structural Verilog: 1 circuit, main circuit main
module main (
  input  A,
  input  C,
  output out_3
);

  wire not_1_out;

  not not_1 (not_1_out, A);
  or or_1 (out_3, not_1_out, C);

  // Notes on the sheet:
  //   A'+C
endmodule
