// Logisim project 10c.circ as structural Verilog: 1 circuit, main circuit main
module main (
  input  A,
  input  B,
  input  C,
  output out_4
);

  wire and_1_out, and_2_out, not_1_out, not_2_out, or_1_out, or_2_out;

  not not_1 (not_1_out, C);
  not not_2 (not_2_out, B);
  and and_1 (and_1_out, B, C);
  and and_2 (and_2_out, not_1_out, not_2_out);
  buf or_1 (or_1_out, A);  // OR_Gate
  or or_2 (or_2_out, and_1_out, and_2_out);
  or or_3 (out_4, or_1_out, or_2_out);

  // Notes on the sheet:
  //   A+B'C'+BC
endmodule
