// Logisim project 01.circ as structural Verilog: 1 circuit, main circuit main
module main (
  input  _0,
  input  _1,
  input  _2,
  input  _3,
  input  _4,
  input  _5,
  input  _6,
  input  x0,
  input  x1,
  input  x2,
  input  _7,
  output out
);

  wire multiplexer_1_out, multiplexer_2_out, multiplexer_3_out, multiplexer_4_out, multiplexer_5_out,
       multiplexer_6_out;

  Multiplexer #(.enable("false")) multiplexer_1 (.in0(_0), .in1(_1), .out(multiplexer_1_out), .sel(x2));
  Multiplexer #(.enable("false")) multiplexer_2 (.in0(_2), .in1(_3), .out(multiplexer_2_out), .sel(x2));
  Multiplexer #(.enable("false")) multiplexer_3 (.in0(_4), .in1(_5), .out(multiplexer_3_out), .sel(x2));
  Multiplexer #(.enable("false")) multiplexer_4 (.in0(_6), .in1(_7), .out(multiplexer_4_out), .sel(x2));
  Multiplexer #(.enable("false")) multiplexer_5 (
    .in0(multiplexer_1_out), .in1(multiplexer_2_out), .out(multiplexer_5_out), .sel(x1));
  Multiplexer #(.enable("false")) multiplexer_6 (
    .in0(multiplexer_3_out), .in1(multiplexer_4_out), .out(multiplexer_6_out), .sel(x1));
  Multiplexer #(.enable("false")) multiplexer_7 (.in0(multiplexer_5_out), .in1(multiplexer_6_out), .out(out), .sel(x0));
endmodule
