// Logisim project 02.circ as structural Verilog: 1 circuit, main circuit main
module main (
  input  [7:0] in_1,
  input  [7:0] in_2,
  output [3:0] out_3,
  output out_4
);

  wire priority_encoder_1_gs;
  wire [2:0] priority_encoder_1_out, priority_encoder_2_out;

  Priority_Encoder priority_encoder_1 (
    .in0(in_1[0]), .in1(in_1[1]), .in2(in_1[2]), .in3(in_1[3]), .in4(in_1[4]), .in5(in_1[5]), .in6(in_1[6]),
    .in7(in_1[7]), .out(priority_encoder_1_out), .gs(priority_encoder_1_gs));  // open: en_in, en_out
  Priority_Encoder priority_encoder_2 (
    .in0(in_2[0]), .in1(in_2[1]), .in2(in_2[2]), .in3(in_2[3]), .in4(in_2[4]), .in5(in_2[5]), .in6(in_2[6]),
    .in7(in_2[7]), .out(priority_encoder_2_out), .gs(out_3[3]));  // open: en_in, en_out
  Multiplexer #(.width(3), .enable("false")) multiplexer_1 (
    .in0(priority_encoder_1_out), .in1(priority_encoder_2_out), .out(out_3[2:0]), .sel(out_3[3]));
  or or_1 (out_4, priority_encoder_1_gs, out_3[3]);
endmodule
