// Logisim project 03.circ as structural Verilog: 1 circuit, main circuit main
module main (
  output out_1,
  output out_2,
  output out_3
);

  wire clock_1_out;
  wire [2:0] rom_1_data;

  Clock clock_1 (.out(clock_1_out));
  ROM #(.addrWidth(3), .dataWidth(3)) rom_1 (.addr({out_3, out_2, out_1}), .data(rom_1_data));  // open: sel
  D_Flip_Flop d_ff_1 (.clk(clock_1_out), .D(rom_1_data[0]), .Q(out_1));  // open: Qn, preset, en, reset
  D_Flip_Flop d_ff_2 (.clk(clock_1_out), .D(rom_1_data[1]), .Q(out_2));  // open: Qn, preset, en, reset
  D_Flip_Flop d_ff_3 (.clk(clock_1_out), .D(rom_1_data[2]), .Q(out_3));  // open: Qn, preset, en, reset

  // Notes on the sheet:
  //   contents of rom_1 (hex, n*v repeats v):
  //   1 2 3 4 5 6
endmodule
