// Logisim project 05.circ as structural Verilog: 1 circuit, main circuit main
module main (
  input  in_1,
  input  B,
  input  A,
  input  B_2,
  input  A_2,
  input  B_3,
  input  A_3,
  input  B_4,
  input  A_4,
  input  B_5,
  input  A_5,
  input  B_6,
  input  A_6,
  input  B_7,
  input  A_7,
  input  B_8,
  input  A_8,
  output out_18,
  output out_19,
  output out_20,
  output out_21,
  output out_22,
  output out_23,
  output out_24,
  output out_25,
  output out_26
);

  wire and_1_out, and_2_out, and_3_out, and_4_out, and_5_out, and_6_out, and_7_out, and_8_out, and_9_out,
       and_10_out, and_11_out, and_12_out, and_13_out, and_14_out, and_15_out, and_16_out, or_1_out,
       or_2_out, or_3_out, or_4_out, or_5_out, or_6_out, or_7_out, xor_1_out, xor_2_out, xor_3_out,
       xor_4_out, xor_5_out, xor_6_out, xor_7_out, xor_8_out, xor_9_out, xor_10_out, xor_11_out, xor_12_out,
       xor_13_out, xor_14_out, xor_15_out, xor_16_out;

  xor xor_1 (xor_1_out, in_1, A);
  xor xor_2 (xor_2_out, in_1, A_2);
  xor xor_3 (xor_3_out, in_1, A_3);
  xor xor_4 (xor_4_out, in_1, A_4);
  xor xor_5 (xor_5_out, in_1, A_5);
  xor xor_6 (xor_6_out, in_1, A_6);
  xor xor_7 (xor_7_out, in_1, A_7);
  xor xor_8 (xor_8_out, in_1, A_8);
  xor xor_9 (xor_9_out, B, xor_1_out);
  and and_1 (and_1_out, B, xor_1_out);
  xor xor_10 (xor_10_out, B_2, xor_2_out);
  and and_2 (and_2_out, B_2, xor_2_out);
  xor xor_11 (xor_11_out, B_3, xor_3_out);
  and and_3 (and_3_out, B_3, xor_3_out);
  xor xor_12 (xor_12_out, B_4, xor_4_out);
  and and_4 (and_4_out, B_4, xor_4_out);
  xor xor_13 (xor_13_out, B_5, xor_5_out);
  and and_5 (and_5_out, B_5, xor_5_out);
  xor xor_14 (xor_14_out, B_6, xor_6_out);
  and and_6 (and_6_out, B_6, xor_6_out);
  xor xor_15 (xor_15_out, B_7, xor_7_out);
  and and_7 (and_7_out, B_7, xor_7_out);
  xor xor_16 (xor_16_out, B_8, xor_8_out);
  and and_8 (and_8_out, B_8, xor_8_out);
  xor xor_17 (out_18, xor_9_out, in_1);
  and and_9 (and_9_out, xor_9_out, in_1);
  xor xor_18 (out_19, xor_10_out, or_1_out);
  and and_10 (and_10_out, xor_10_out, or_1_out);
  xor xor_19 (out_20, xor_11_out, or_2_out);
  and and_11 (and_11_out, xor_11_out, or_2_out);
  xor xor_20 (out_21, xor_12_out, or_3_out);
  and and_12 (and_12_out, xor_12_out, or_3_out);
  xor xor_21 (out_22, xor_13_out, or_4_out);
  and and_13 (and_13_out, xor_13_out, or_4_out);
  xor xor_22 (out_23, xor_14_out, or_5_out);
  and and_14 (and_14_out, xor_14_out, or_5_out);
  xor xor_23 (out_24, xor_15_out, or_6_out);
  and and_15 (and_15_out, xor_15_out, or_6_out);
  xor xor_24 (out_25, xor_16_out, or_7_out);
  and and_16 (and_16_out, xor_16_out, or_7_out);
  or or_1 (or_1_out, and_9_out, and_1_out);
  or or_2 (or_2_out, and_10_out, and_2_out);
  or or_3 (or_3_out, and_11_out, and_3_out);
  or or_4 (or_4_out, and_12_out, and_4_out);
  or or_5 (or_5_out, and_13_out, and_5_out);
  or or_6 (or_6_out, and_14_out, and_6_out);
  or or_7 (or_7_out, and_15_out, and_7_out);
  or or_8 (out_26, and_16_out, and_8_out);
endmodule
