// Logisim project 10a.circ as structural Verilog: 1 circuit, main circuit main
module main (
  input  B,
  input  C,
  output out_3
);

  wire and_1_out, and_2_out, not_1_out, not_2_out;

  not not_1 (not_1_out, B);
  not not_2 (not_2_out, C);
  and and_1 (and_1_out, not_1_out, C);
  and and_2 (and_2_out, not_2_out, B);
  or or_1 (out_3, and_1_out, and_2_out);

  // Notes on the sheet:
  //   B'C+BC'
endmodule
