// Logisim project OneAddress.circ as structural Verilog: 5 circuits, main circuit Control Unit
module Control_Unit (
  input  [7:0] Instruction,
  output [3:0] ALUOp,
  output IMM,
  output MEM,
  output CLRAC,
  output WRMEM,
  output BEQ,
  output B
);

  ROM #(.addrWidth(4), .dataWidth(6)) rom_1 (
    .addr(Instruction[7:4]), .data({B, BEQ, WRMEM, CLRAC, MEM, IMM}));  // open: sel

  assign ALUOp = Instruction[3:0];

  // Notes on the sheet:
  //   contents of rom_1 (hex, n*v repeats v):
  //   0 3 1 5 8 10
endmodule

module SignExtend (
  input  [7:0] Immediate,
  output [15:0] SignExtValue
);


  assign SignExtValue = {{9{Immediate[7]}}, Immediate[6:0]};
endmodule

module CPU_Main (
);

  wire and_1_out, button_1_out, clock_1_out, comparator_1_eq, control_unit_1_b, control_unit_1_beq,
       control_unit_1_clrac, control_unit_1_imm, control_unit_1_mem, control_unit_1_wrmem, or_1_out;
  wire [3:0] control_unit_1_aluop;
  wire [7:0] adder_1_out, multiplexer_1_out, PC_q;
  wire [15:0] AC_q, alu_1_output, multiplexer_2_out, multiplexer_3_out, ram_1_data, ram_2_data,
       signextend_1_signextvalue;

  Clock clock_1 (.out(clock_1_out));
  Button button_1 (.out(button_1_out));
  Adder adder_1 (.a(PC_q), .b(8'h1), .out(adder_1_out));  // open: cin, cout
  or or_1 (or_1_out, and_1_out, control_unit_1_b);
  and and_1 (and_1_out, comparator_1_eq, control_unit_1_beq);
  Multiplexer #(.width(8), .enable("false")) multiplexer_1 (
    .in0(adder_1_out), .in1(ram_1_data[7:0]), .out(multiplexer_1_out), .sel(or_1_out));
  Register PC (.D(multiplexer_1_out), .en(1'b1), .Q(PC_q), .clk(clock_1_out), .clr(button_1_out));
  RAM #(.dataWidth(16)) ram_1 (.addr(PC_q), .data(ram_1_data), .clk(clock_1_out));  // open: sel, ld, clr
  Control_Unit control_unit_1 (
    .Instruction(ram_1_data[15:8]), .ALUOp(control_unit_1_aluop), .IMM(control_unit_1_imm),
    .MEM(control_unit_1_mem), .CLRAC(control_unit_1_clrac), .WRMEM(control_unit_1_wrmem),
    .BEQ(control_unit_1_beq), .B(control_unit_1_b));
  RAM #(.dataWidth(16), .bus("separate")) ram_2 (
    .addr(ram_1_data[7:0]), .din(AC_q), .data(ram_2_data), .str(control_unit_1_wrmem), .sel(1'b1),
    .clk(clock_1_out), .ld(1'b1));  // open: clr
  SignExtend signextend_1 (.Immediate(ram_1_data[7:0]), .SignExtValue(signextend_1_signextvalue));
  Multiplexer #(.width(16), .enable("false")) multiplexer_2 (
    .in0(alu_1_output), .in1({16{1'b0}}), .out(multiplexer_2_out), .sel(control_unit_1_clrac));
  Register #(.width(16)) AC (
    .D(multiplexer_2_out), .en(control_unit_1_imm), .Q(AC_q), .clk(clock_1_out), .clr(button_1_out));
  Multiplexer #(.width(16), .enable("false")) multiplexer_3 (
    .in0(ram_2_data), .in1(signextend_1_signextvalue), .out(multiplexer_3_out), .sel(control_unit_1_mem));
  Comparator #(.width(16)) comparator_1 (.a(AC_q), .b({16{1'b0}}), .eq(comparator_1_eq));  // open: gt, lt
  ALU alu_1 (.AC(AC_q), .Y(multiplexer_3_out), .ALUOp(control_unit_1_aluop), .Output(alu_1_output));

  // Notes on the sheet:
  //   Reset PC
  //   Increment PC
  //   Branch Address
  //   Next Instr
  //   select if branch = true and ALU is zero
  //   Text (Program) Memory
  //   unconditional branch
  //   Control Unit
  //   Data Memory
  //   Sign Extend
  //   AC to Memory
  //   Mem Data
  //   Immediate
  //   Select ALU Input
  //   AC to ALU
  //   ALU to AC
  //   ALU
  //   ALUOpt
endmodule

module ALU (
  input  [15:0] AC,
  input  [15:0] Y,
  input  [3:0] ALUOp,
  output [15:0] Output
);

  wire [15:0] adder_1_out, alu_bitwise_add_1_output, divider_1_out, divider_1_rem, multiplier_1_out,
       shifter_1_out, subtractor_1_out;

  Adder #(.width(16)) adder_1 (.a(AC), .b(Y), .out(adder_1_out));  // open: cin, cout
  Subtractor #(.width(16)) subtractor_1 (.a(AC), .b(Y), .out(subtractor_1_out));  // open: bin, bout
  Multiplier #(.width(16)) multiplier_1 (.a(AC), .b(Y), .out(multiplier_1_out));  // open: cin, cout
  Divider #(.width(16)) divider_1 (.a(AC), .b(Y), .out(divider_1_out), .rem(divider_1_rem));  // open: upper
  ALU_bitwise_add alu_bitwise_add_1 (.AC(AC), .Y(Y), .Output(alu_bitwise_add_1_output));
  Shifter #(.width(16)) shifter_1 (.in(AC), .\dist (Y[3:0]), .out(shifter_1_out));
  Multiplexer #(.select(4), .width(16), .enable("false")) multiplexer_1 (
    .in0(adder_1_out), .in1(subtractor_1_out), .in2(multiplier_1_out), .in3(divider_1_out),
    .in4(divider_1_rem), .in5(alu_bitwise_add_1_output), .in6(shifter_1_out), .out(Output), .sel(ALUOp));  // open: in7, in8, in9, in10, in11, in12, in13, in14, in15
  // also tied to GND on the sheet: {Y[4], Y[5], Y[6], Y[7], Y[8], Y[9], Y[10], Y[11], Y[12], Y[13], Y[14], Y[15]}

  // Notes on the sheet:
  //   0000 = add
  //   0001 = sub
  //   0002 = mul
  //   0003 = div
  //   0004 = rem
  //   0005 = and
  //   0006 = shift
endmodule

// and
module ALU_bitwise_add (
  input  [15:0] AC,
  input  [15:0] Y,
  output [15:0] Output
);

  and and_1 (Output[0], Y[0], AC[0]);
  and and_2 (Output[1], Y[1], AC[1]);
  and and_3 (Output[2], AC[2], Y[2]);
  and and_4 (Output[3], Y[3], AC[3]);
  and and_5 (Output[4], AC[4], Y[4]);
  and and_6 (Output[5], AC[5], Y[5]);
  and and_7 (Output[6], Y[6], AC[6]);
  and and_8 (Output[7], AC[7], Y[7]);
  and and_9 (Output[8], AC[8], Y[8]);
  and and_10 (Output[9], AC[9], Y[9]);
  and and_11 (Output[10], Y[10], AC[10]);
  and and_12 (Output[11], AC[11], Y[11]);
  and and_13 (Output[12], AC[12], Y[12]);
  and and_14 (Output[13], AC[13], Y[13]);
  and and_15 (Output[14], Y[14], AC[14]);
  and and_16 (Output[15], AC[15], Y[15]);
endmodule
