// Logisim project 02.circ as structural Verilog: 1 circuit, main circuit main
module main (
  input  [7:0] _0_7,
  input  [7:0] _8_15,
  output [3:0] out,
  output on
);

  wire priority_encoder_1_gs;
  wire [2:0] priority_encoder_1_out, priority_encoder_2_out;

  Priority_Encoder priority_encoder_1 (
    .in0(_0_7[0]), .in1(_0_7[1]), .in2(_0_7[2]), .in3(_0_7[3]), .in4(_0_7[4]), .in5(_0_7[5]), .in6(_0_7[6]),
    .in7(_0_7[7]), .out(priority_encoder_1_out), .gs(priority_encoder_1_gs));  // open: en_in, en_out
  Priority_Encoder priority_encoder_2 (
    .in0(_8_15[0]), .in1(_8_15[1]), .in2(_8_15[2]), .in3(_8_15[3]), .in4(_8_15[4]), .in5(_8_15[5]),
    .in6(_8_15[6]), .in7(_8_15[7]), .out(priority_encoder_2_out), .gs(out[3]));  // open: en_in, en_out
  Multiplexer #(.width(3), .enable("false")) multiplexer_1 (
    .in0(priority_encoder_1_out), .in1(priority_encoder_2_out), .out(out[2:0]), .sel(out[3]));
  or or_1 (on, priority_encoder_1_gs, out[3]);
endmodule
